// Logisim project Small decoder.circ as structural Verilog: 1 circuit, main circuit main
module main (
  input  [7:0] Input_A,
  input  [7:0] Input_B,
  input  [1:0] OP_code,
  output [7:0] Result
);

  wire [7:0] adder_1_out, divider_1_out, multiplier_1_out, subtractor_1_out;

  Adder adder_1 (.a(Input_A), .b(Input_B), .out(adder_1_out));  // open: cin, cout
  Subtractor subtractor_1 (.a(Input_A), .b(Input_B), .out(subtractor_1_out));  // open: bin, bout
  Multiplier multiplier_1 (.a(Input_A), .b(Input_B), .out(multiplier_1_out));  // open: cin, cout
  Divider divider_1 (.a(Input_A), .b(Input_B), .out(divider_1_out));  // open: upper, rem
  Multiplexer #(.select(2), .width(8), .enable("false")) multiplexer_1 (
    .in0(adder_1_out), .in1(subtractor_1_out), .in2(multiplier_1_out), .in3(divider_1_out), .out(Result),
    .sel(OP_code));

  // Notes on the sheet:
  //   Decoder
endmodule
