// Logisim project cpuProject.circ as structural Verilog: 4 circuits, main circuit main
module main (
  input  Clear
);

  wire clock_1_out;
  wire [1:0] decoder_1_operand_1, decoder_1_operand_2;
  wire [9:0] ram_1_data;

  Decoder decoder_1 (
    .in_1(ram_1_data), .operand_2(decoder_1_operand_2), .operand_1(decoder_1_operand_1));  // open: operand_3, op
  ALU alu_1 ();  // open: Input_A, Result, Input_B, OP_code
  Registers registers_1 (
    .Clr(Clear), .operand_1(decoder_1_operand_1), .operand_2(decoder_1_operand_2));  // open: in_1, in_2, Destination, out_7, out_8
  Clock clock_1 (.out(clock_1_out));
  RAM #(.dataWidth(10)) ram_1 (.data(ram_1_data), .clk(clock_1_out));  // open: addr, sel, ld, clr
endmodule

module ALU (
  input  [7:0] Input_A,
  input  [7:0] Input_B,
  input  [2:0] OP_code,
  output [7:0] Result
);

  wire [7:0] adder_1_out, divider_1_out, multiplier_1_out, negator_1_out, subtractor_1_out;

  Adder adder_1 (.a(Input_A), .b(Input_B), .out(adder_1_out));  // open: cin, cout
  Subtractor subtractor_1 (.a(Input_A), .b(Input_B), .out(subtractor_1_out));  // open: bin, bout
  Multiplier multiplier_1 (.a(Input_A), .b(Input_B), .out(multiplier_1_out));  // open: cin, cout
  Divider divider_1 (.a(Input_A), .b(Input_B), .out(divider_1_out));  // open: upper, rem
  Negator negator_1 (.in(Input_A), .out(negator_1_out));
  Multiplexer #(.select(3), .width(8), .enable("false")) multiplexer_1 (
    .in0(adder_1_out), .in1(subtractor_1_out), .in2(multiplier_1_out), .in3(divider_1_out),
    .in4(negator_1_out), .out(Result), .sel(OP_code));  // open: in5, in6, in7

  // Other names for the same wires on the sheet: ALU[7:0] = Result

  // Notes on the sheet:
  //   ALU
endmodule

// REGS
module Registers (
  input  [15:0] in_1,
  input  in_2,
  input  [1:0] Destination,
  input  [1:0] operand_1,
  input  [1:0] operand_2,
  input  Clr,
  output [15:0] out_7,
  output [15:0] out_8
);

  wire demultiplexer_1_out0, demultiplexer_1_out1, demultiplexer_1_out2, demultiplexer_1_out3;
  wire [15:0] R1_q, R2_q, register_1_q, register_2_q;

  Demultiplexer #(.select(2), .enable("false")) demultiplexer_1 (
    .out0(demultiplexer_1_out0), .out1(demultiplexer_1_out1), .out2(demultiplexer_1_out2),
    .out3(demultiplexer_1_out3), .in(in_2), .sel(Destination));
  Register #(.width(16)) R1 (.D(in_1), .Q(R1_q), .clk(demultiplexer_1_out0), .clr(Clr));  // open: en
  Register #(.width(16)) R2 (.D(in_1), .Q(R2_q), .clk(demultiplexer_1_out1), .clr(Clr));  // open: en
  Register #(.width(16)) register_1 (.D(in_1), .Q(register_1_q), .clk(demultiplexer_1_out2), .clr(Clr));  // open: en
  Register #(.width(16)) register_2 (.D(in_1), .Q(register_2_q), .clk(demultiplexer_1_out3), .clr(Clr));  // open: en
  Multiplexer #(.select(2), .width(16), .enable("false")) multiplexer_1 (
    .in0(R1_q), .in1(R2_q), .in2(register_1_q), .in3(register_2_q), .out(out_7), .sel(operand_1));
  Multiplexer #(.select(2), .width(16), .enable("false")) multiplexer_2 (
    .in0(R1_q), .in1(R2_q), .in2(register_1_q), .in3(register_2_q), .out(out_8), .sel(operand_2));
endmodule

// DECODER
module Decoder (
  input  [9:0] in_1,
  output [1:0] operand_3,
  output [1:0] operand_2,
  output [1:0] operand_1,
  output [3:0] op
);


  assign op = in_1[9:6];
  assign operand_1 = in_1[5:4];
  assign operand_2 = in_1[3:2];
  assign operand_3 = in_1[1:0];

  // Notes on the sheet:
  //   move
  //   copy
  //   delete
  //   add
  //   subtract
  //   multiply
  //   divide
  //   invert
  //   Decoder
endmodule
